// Logisim project DRRIP.circ as structural Verilog: 1 circuit, main circuit main
module main (
  input  [3:0] tag_in,
  input  acesso_valido,
  input  SRRIP_1__ou_BRRIP_0,
  output hit0,
  output hit1,
  output eh_hit,
  output hit2,
  output hit3,
  output [1:0] via_hit,
  output invalid0,
  output invalid1,
  output invalido,
  output invalid2,
  output invalid3,
  output miss_update,
  output [1:0] via_invalida,
  output [1:0] rrpv0_next,
  output vitima0,
  output rrpv0_igual_3,
  output [1:0] rrpv1_next,
  output rrpv1_igual_3,
  output vitima1,
  output [1:0] via_vitima,
  output rrpv_igual_3,
  output rrpv2_igual_3,
  output [1:0] rrpv0_hit,
  output [1:0] rrpv2_next,
  output rrpv3_igual_3,
  output vitima2,
  output vitima_encontrada,
  output [1:0] rrpv1_hit,
  output [1:0] rrpv3_next,
  output vitima3,
  output [1:0] rrpv2_hit,
  output [1:0] via_rrpv3,
  output envelhecer_rrpvs,
  output [1:0] rrpv3_hit,
  output [1:0] idade_rrpv0,
  output [1:0] rrpv0___1,
  output rrpv0___3,
  output [1:0] prox_rrpv0,
  output [1:0] rrpv1___1,
  output rrpv1___3,
  output [1:0] idade_rrpv1,
  output [1:0] prox_rrpv1,
  output [1:0] rrpv2___1,
  output rrpv2___3,
  output [1:0] idade_rrpv2,
  output [1:0] prox_rrpv2,
  output [1:0] rrpv3___1,
  output rrpv3___3,
  output [1:0] idade_rrpv3,
  output [1:0] prox_rrpv3,
  output [1:0] insercao_rrpv
);

  wire and_1_out, and_2_out, and_3_out, and_8_out, and_9_out, clock_1_out, comparator_1_eq, comparator_2_eq,
       comparator_3_eq, comparator_4_eq, comparator_13_eq, comparator_14_eq, comparator_15_eq,
       comparator_16_eq, enable_tag_out, grava_tag0_out, grava_tag1_out, grava_tag2_out, grava_tag3_out,
       multiplexer_5_out, multiplexer_6_out, multiplexer_7_out, multiplexer_8_out, not_5_out, not_6_out,
       not_7_out, not_8_out, not_9_out, not_10_out, or_1_out, or_2_out, or_7_out, valid0_q, valid1_q,
       valid2_q, valid3_q;
  wire [1:0] rrpv0_q, rrpv1_q, rrpv2_q, rrpv3_q;
  wire [3:0] multiplexer_1_out, multiplexer_2_out, multiplexer_3_out, multiplexer_4_out, tag0_q, tag1_q,
       tag2_q, tag3_q;

  or or_1 (or_1_out, eh_hit, miss_update, envelhecer_rrpvs);
  and and_1 (and_1_out, or_1_out, acesso_valido);
  and enable_tag (enable_tag_out, acesso_valido, miss_update);
  Clock clock_1 (.out(clock_1_out));
  and grava_tag0 (grava_tag0_out, vitima0, enable_tag_out);
  and grava_tag1 (grava_tag1_out, vitima1, enable_tag_out);
  and grava_tag2 (grava_tag2_out, vitima2, enable_tag_out);
  and grava_tag3 (grava_tag3_out, vitima3, enable_tag_out);
  Register #(.width(2)) rrpv0 (.D(rrpv0_next), .en(and_1_out), .Q(rrpv0_q), .clk(clock_1_out));  // open: clr
  Register #(.width(2)) rrpv1 (.D(rrpv1_next), .en(and_1_out), .Q(rrpv1_q), .clk(clock_1_out));  // open: clr
  Register #(.width(2)) rrpv2 (.D(rrpv2_next), .en(and_1_out), .Q(rrpv2_q), .clk(clock_1_out));  // open: clr
  Register #(.width(2)) rrpv3 (.D(rrpv3_next), .en(and_1_out), .Q(rrpv3_q), .clk(clock_1_out));  // open: clr
  Multiplexer #(.width(4)) multiplexer_1 (
    .in0(tag0_q), .in1(tag_in), .out(multiplexer_1_out), .sel(grava_tag0_out));  // open: en
  Multiplexer #(.width(4)) multiplexer_2 (
    .in0(tag1_q), .in1(tag_in), .out(multiplexer_2_out), .sel(grava_tag1_out));  // open: en
  Multiplexer #(.width(4)) multiplexer_3 (
    .in0(tag2_q), .in1(tag_in), .out(multiplexer_3_out), .sel(grava_tag2_out));  // open: en
  Multiplexer #(.width(4)) multiplexer_4 (
    .in0(tag3_q), .in1(tag_in), .out(multiplexer_4_out), .sel(grava_tag3_out));  // open: en
  Multiplexer multiplexer_5 (.in0(valid0_q), .in1(1'b1), .out(multiplexer_5_out), .sel(grava_tag0_out));  // open: en
  Multiplexer multiplexer_6 (.in0(valid1_q), .in1(1'b1), .out(multiplexer_6_out), .sel(grava_tag1_out));  // open: en
  Multiplexer multiplexer_7 (.in0(valid2_q), .in1(1'b1), .out(multiplexer_7_out), .sel(grava_tag2_out));  // open: en
  Multiplexer multiplexer_8 (.in0(valid3_q), .in1(1'b1), .out(multiplexer_8_out), .sel(grava_tag3_out));  // open: en
  Register #(.width(4)) tag0 (.D(multiplexer_1_out), .en(enable_tag_out), .Q(tag0_q), .clk(clock_1_out));  // open: clr
  Register #(.width(4)) tag1 (.D(multiplexer_2_out), .en(enable_tag_out), .Q(tag1_q), .clk(clock_1_out));  // open: clr
  Register #(.width(4)) tag2 (.D(multiplexer_3_out), .en(enable_tag_out), .Q(tag2_q), .clk(clock_1_out));  // open: clr
  Register #(.width(4)) tag3 (.D(multiplexer_4_out), .en(enable_tag_out), .Q(tag3_q), .clk(clock_1_out));  // open: clr
  Register #(.width(1)) valid0 (
    .D(multiplexer_5_out), .en(enable_tag_out), .Q(valid0_q), .clk(clock_1_out));  // open: clr
  Register #(.width(1)) valid1 (
    .D(multiplexer_6_out), .en(enable_tag_out), .Q(valid1_q), .clk(clock_1_out));  // open: clr
  Register #(.width(1)) valid2 (
    .D(multiplexer_7_out), .en(enable_tag_out), .Q(valid2_q), .clk(clock_1_out));  // open: clr
  Register #(.width(1)) valid3 (
    .D(multiplexer_8_out), .en(enable_tag_out), .Q(valid3_q), .clk(clock_1_out));  // open: clr
  Comparator #(.width(4)) comparator_1 (.a(tag_in), .b(tag0_q), .eq(comparator_1_eq));  // open: gt, lt
  Comparator #(.width(4)) comparator_2 (.a(tag_in), .b(tag1_q), .eq(comparator_2_eq));  // open: gt, lt
  Comparator #(.width(4)) comparator_3 (.a(tag_in), .b(tag2_q), .eq(comparator_3_eq));  // open: gt, lt
  Comparator #(.width(4)) comparator_4 (.a(tag_in), .b(tag3_q), .eq(comparator_4_eq));  // open: gt, lt
  Comparator #(.width(2)) comparator_5 (.a(2'b11), .b(rrpv0_q), .eq(rrpv0_igual_3));  // open: gt, lt
  Comparator #(.width(2)) comparator_6 (.a(2'b11), .b(rrpv1_q), .eq(rrpv1_igual_3));  // open: gt, lt
  Comparator #(.width(2)) comparator_7 (.a(2'b11), .b(rrpv2_q), .eq(rrpv2_igual_3));  // open: gt, lt
  Comparator #(.width(2)) comparator_8 (.a(2'b11), .b(rrpv3_q), .eq(rrpv3_igual_3));  // open: gt, lt
  Comparator #(.width(2), .mode("unsigned")) comparator_9 (.a(rrpv0_q), .b(2'b11), .lt(rrpv0___3));  // open: gt, eq
  Comparator #(.width(2), .mode("unsigned")) comparator_10 (.a(rrpv1_q), .b(2'b11), .lt(rrpv1___3));  // open: gt, eq
  Comparator #(.width(2), .mode("unsigned")) comparator_11 (.a(rrpv2_q), .b(2'b11), .lt(rrpv2___3));  // open: gt, eq
  Comparator #(.width(2), .mode("unsigned")) comparator_12 (.a(rrpv3_q), .b(2'b11), .lt(rrpv3___3));  // open: gt, eq
  not not_1 (invalid0, valid0_q);
  not not_2 (invalid1, valid1_q);
  not not_3 (invalid2, valid2_q);
  not not_4 (invalid3, valid3_q);
  not not_5 (not_5_out, rrpv0_igual_3);
  not not_6 (not_6_out, rrpv1_igual_3);
  not not_7 (not_7_out, rrpv2_igual_3);
  Multiplexer #(.width(2)) multiplexer_9 (
    .in0(2'b11), .in1(2'b10), .out(insercao_rrpv), .sel(SRRIP_1__ou_BRRIP_0));  // open: en
  or or_2 (or_2_out, rrpv2_igual_3, rrpv3_igual_3);
  and and_2 (and_2_out, not_5_out, rrpv1_igual_3);
  and and_3 (and_3_out, not_5_out, not_6_out, not_7_out, rrpv3_igual_3);
  and and_4 (hit0, comparator_1_eq, valid0_q);
  and and_5 (hit1, comparator_2_eq, valid1_q);
  and and_6 (hit2, comparator_3_eq, valid2_q);
  and and_7 (hit3, comparator_4_eq, valid3_q);
  and and_8 (and_8_out, valid0_q, invalid1);
  and and_9 (and_9_out, valid0_q, valid1_q, valid2_q, invalid3);
  or or_3 (rrpv_igual_3, rrpv0_igual_3, rrpv1_igual_3, rrpv2_igual_3, rrpv3_igual_3);
  and via_rrpv3__1 (via_rrpv3[1], or_2_out, not_5_out, not_6_out);
  or via_rrpv3__0 (via_rrpv3[0], and_2_out, and_3_out);
  Adder #(.width(2)) adder_1 (.a(rrpv0_q), .b(2'b01), .out(rrpv0___1));  // open: cin, cout
  Adder #(.width(2)) adder_2 (.a(rrpv1_q), .b(2'b01), .out(rrpv1___1));  // open: cin, cout
  Adder #(.width(2)) adder_3 (.a(rrpv2_q), .b(2'b01), .out(rrpv2___1));  // open: cin, cout
  Adder #(.width(2)) adder_4 (.a(rrpv3_q), .b(2'b01), .out(rrpv3___1));  // open: cin, cout
  or via_invalida_0 (via_invalida[0], and_8_out, and_9_out);
  or or_4 (via_hit[1], hit2, hit3);
  or or_5 (via_hit[0], hit1, hit3);
  or or_6 (invalido, invalid0, invalid1, invalid2, invalid3);
  or or_7 (or_7_out, invalid2, invalid3);
  or or_8 (eh_hit, hit0, hit1, hit2, hit3);
  and via_invalida_1 (via_invalida[1], valid0_q, valid1_q, or_7_out);
  Multiplexer #(.width(2)) multiplexer_10 (
    .in0(2'b11), .in1(rrpv0___1), .out(prox_rrpv0), .sel(rrpv0___3));  // open: en
  Multiplexer #(.width(2)) multiplexer_11 (
    .in0(2'b11), .in1(rrpv1___1), .out(prox_rrpv1), .sel(rrpv1___3));  // open: en
  Multiplexer #(.width(2)) multiplexer_12 (
    .in0(2'b11), .in1(rrpv2___1), .out(prox_rrpv2), .sel(rrpv2___3));  // open: en
  Multiplexer #(.width(2)) multiplexer_13 (
    .in0(2'b11), .in1(rrpv3___1), .out(prox_rrpv3), .sel(rrpv3___3));  // open: en
  not not_8 (not_8_out, invalido);
  not not_9 (not_9_out, rrpv_igual_3);
  and and_10 (envelhecer_rrpvs, not_8_out, not_9_out);
  Multiplexer #(.width(2)) multiplexer_14 (
    .in0(via_rrpv3), .in1(via_invalida), .out(via_vitima), .sel(invalido));  // open: en
  or or_9 (vitima_encontrada, invalido, rrpv_igual_3);
  Multiplexer #(.width(2)) multiplexer_15 (
    .in0(rrpv0_q), .in1(prox_rrpv0), .out(idade_rrpv0), .sel(envelhecer_rrpvs));  // open: en
  Multiplexer #(.width(2)) multiplexer_16 (
    .in0(rrpv1_q), .in1(prox_rrpv1), .out(idade_rrpv1), .sel(envelhecer_rrpvs));  // open: en
  Multiplexer #(.width(2)) multiplexer_17 (
    .in0(rrpv2_q), .in1(prox_rrpv2), .out(idade_rrpv2), .sel(envelhecer_rrpvs));  // open: en
  Multiplexer #(.width(2)) multiplexer_18 (
    .in0(rrpv3_q), .in1(prox_rrpv3), .out(idade_rrpv3), .sel(envelhecer_rrpvs));  // open: en
  Multiplexer #(.width(2)) multiplexer_19 (.in0(idade_rrpv0), .in1(2'b00), .out(rrpv0_hit), .sel(hit0));  // open: en
  Multiplexer #(.width(2)) multiplexer_20 (.in0(idade_rrpv1), .in1(2'b00), .out(rrpv1_hit), .sel(hit1));  // open: en
  Multiplexer #(.width(2)) multiplexer_21 (.in0(idade_rrpv2), .in1(2'b00), .out(rrpv2_hit), .sel(hit2));  // open: en
  Multiplexer #(.width(2)) multiplexer_22 (.in0(idade_rrpv3), .in1(2'b00), .out(rrpv3_hit), .sel(hit3));  // open: en
  not not_10 (not_10_out, eh_hit);
  and and_11 (miss_update, not_10_out, vitima_encontrada);
  Comparator #(.width(2), .mode("unsigned")) comparator_13 (
    .a(via_vitima), .b(2'b00), .eq(comparator_13_eq));  // open: gt, lt
  Comparator #(.width(2), .mode("unsigned")) comparator_14 (
    .a(via_vitima), .b(2'b01), .eq(comparator_14_eq));  // open: gt, lt
  Comparator #(.width(2), .mode("unsigned")) comparator_15 (
    .a(via_vitima), .b(2'b10), .eq(comparator_15_eq));  // open: gt, lt
  Comparator #(.width(2), .mode("unsigned")) comparator_16 (
    .a(via_vitima), .b(2'b11), .eq(comparator_16_eq));  // open: gt, lt
  and and_12 (vitima0, comparator_13_eq, miss_update);
  and and_13 (vitima1, comparator_14_eq, miss_update);
  and and_14 (vitima2, comparator_15_eq, miss_update);
  and and_15 (vitima3, comparator_16_eq, miss_update);
  Multiplexer #(.width(2)) multiplexer_23 (
    .in0(rrpv0_hit), .in1(insercao_rrpv), .out(rrpv0_next), .sel(vitima0));  // open: en
  Multiplexer #(.width(2)) multiplexer_24 (
    .in0(rrpv1_hit), .in1(insercao_rrpv), .out(rrpv1_next), .sel(vitima1));  // open: en
  Multiplexer #(.width(2)) multiplexer_25 (
    .in0(rrpv2_hit), .in1(insercao_rrpv), .out(rrpv2_next), .sel(vitima2));  // open: en
  Multiplexer #(.width(2)) multiplexer_26 (
    .in0(rrpv3_hit), .in1(insercao_rrpv), .out(rrpv3_next), .sel(vitima3));  // open: en
endmodule
